# Fritzing sketch color-sensor (saved by Fritzing 0.9.3b)
breadboards: 1

parts:
  Part1 = IoT WiFi Uno
  e-radionica1 = TCS230 Color Sensor [part_number=101209]

nets:
  N1: Part1.GPIO16, e-radionica1.S1
  5V: Part1.GPIO2, Part1.GPIO10, Part1.GPIO15, Part1.RST, Part1.5V, Part1.GPIO05, e-radionica1.S3, e-radionica1.S2, e-radionica1.Out, e-radionica1.Vcc
  N2: Part1.MOSI, e-radionica1.S0
  GND: Part1.GND, e-radionica1.Gnd

custom parts:
  IoT WiFi Uno: ESP8266 WiFi Uno board
  TCS230 Color Sensor: TCS230
