# Fritzing sketch wifi-uno-led-matrix-max7219 (saved by Fritzing 0.9.3b)
breadboards: 1

parts:
  Part1 = IoT WiFi Uno
  8x8_LED_Modul_mit_MAX1 = 8x8 LED Modul mit MAX7219 [package=THT]

nets:
  N1: Part1.GPIO2, 8x8_LED_Modul_mit_MAX1.CS_Eingang
  N2: Part1.GPIO13, Part1.GND#88, 8x8_LED_Modul_mit_MAX1.DIN_Eingang
  N3: Part1.GPIO12, 8x8_LED_Modul_mit_MAX1.CLK_Eingang
  N4: Part1.3V3, 8x8_LED_Modul_mit_MAX1.VCC_Eingang
  N5: Part1.GND#63, 8x8_LED_Modul_mit_MAX1.GND_Eingang

custom parts:
  IoT WiFi Uno: ESP8266 WiFi Uno board
